# Fritzing sketch SpratMechanismControl (saved by Fritzing 0.8.7b)

parts:
  EtherMega = Arduino Mega 2560 (Rev3)
  12vRelay1 = RELAY [package=relay-jzc]
  12vRelay2 = RELAY [package=relay-jzc]
  12vRelay3 = RELAY [package=relay-jzc]
  12vRelay4 = RELAY [package=relay-jzc]
  12vRelay5 = RELAY [package=relay-jzc]
  12vRelay6 = RELAY [package=relay-jzc]
  12vRelay7 = RELAY [package=relay-jzc]
  12vRelay8 = RELAY [package=relay-jzc]
  13vAdjustablePowerSupply = DC Power [voltage=12V]
  Solenoid_Mirror = Solenoid
  Solenoid_Slit = Solenoid
  Solenoid_Grism = Solenoid
  Solenoid_Grism_Rotate = Solenoid
  SMC_D-C80_#1_Mirror_out = Reed switch [package=THT]
  R1 = Resistor [tolerance=±5% resistance=10k package=THT]
  SMC_D-C80_#2_Mirror_in = Reed switch [package=THT]
  SMC_D-C80_#3_Slit_out = Reed switch [package=THT]
  SMC_D-C80_#4_Slit_in = Reed switch [package=THT]
  SMC_D-C80_#5_Grism_out = Reed switch [package=THT]
  SMC_D-C80_#6_Grism_in = Reed switch [package=THT]
  SMC_D-C80_#7_Grism_Rotation_Pos_0 = Reed switch [package=THT]
  SMC_D-C80_#8_Grism_Rotation_Pos_1 = Reed switch [package=THT]
  R2 = Resistor [tolerance=±5% resistance=10k package=THT]
  R3 = Resistor [tolerance=±5% resistance=10k package=THT]
  R4 = Resistor [tolerance=±5% resistance=10k package=THT]
  R5 = Resistor [tolerance=±5% resistance=10k package=THT]
  R6 = Resistor [tolerance=±5% resistance=10k package=THT]
  R7 = Resistor [tolerance=±5% resistance=10k package=THT]
  R8 = Resistor [tolerance=±5% resistance=10k package=THT]
  Arc_Lamp_Mains_Relay_CARLO_GAVAZZI_-_RGS1A23D25KKE = RELAY [package=relay-jzc]
  Tungsten_Lamp = Filament Lamp [chip_label=? package=THT]
  Arc_Lamp = Filament Lamp [chip_label=? package=THT]
  Mains_Power_plug = Power plug

nets:
  N1: EtherMega.GND, 12vRelay1.COIL1, 12vRelay2.COIL1, 12vRelay3.COIL1, 12vRelay4.COIL1, 12vRelay5.COIL1, 12vRelay6.COIL1, 12vRelay7.COIL1, 12vRelay8.COIL1, R1.Pin_1, R2.Pin_1, R3.Pin_1, R4.Pin_1, R5.Pin_1, R6.Pin_1, R7.Pin_1, R8.Pin_1, Arc_Lamp_Mains_Relay_CARLO_GAVAZZI_-_RGS1A23D25KKE.COIL1
  N2: EtherMega.5V, SMC_D-C80_#1_Mirror_out.pin_2, SMC_D-C80_#2_Mirror_in.pin_2, SMC_D-C80_#3_Slit_out.pin_2, SMC_D-C80_#4_Slit_in.pin_2, SMC_D-C80_#5_Grism_out.pin_2, SMC_D-C80_#6_Grism_in.pin_2, SMC_D-C80_#7_Grism_Rotation_Pos_0.pin_2, SMC_D-C80_#8_Grism_Rotation_Pos_1.pin_2
  N3: EtherMega.D2_PWM, Arc_Lamp_Mains_Relay_CARLO_GAVAZZI_-_RGS1A23D25KKE.COIL2
  N4: EtherMega.D22, 12vRelay1.COIL2
  N5: EtherMega.D23, SMC_D-C80_#1_Mirror_out.pin_1, R1.Pin_0
  N6: EtherMega.D24, 12vRelay2.COIL2
  N7: EtherMega.D25, SMC_D-C80_#2_Mirror_in.pin_1, R2.Pin_0
  N8: EtherMega.D26, 12vRelay3.COIL2
  N9: EtherMega.D27, SMC_D-C80_#3_Slit_out.pin_1, R3.Pin_0
  N10: EtherMega.D28, 12vRelay4.COIL2
  N11: EtherMega.D29, SMC_D-C80_#4_Slit_in.pin_1, R4.Pin_0
  N12: EtherMega.D30, 12vRelay5.COIL2
  N13: EtherMega.D31, SMC_D-C80_#5_Grism_out.pin_1, R5.Pin_0
  N14: EtherMega.D32, 12vRelay6.COIL2
  N15: EtherMega.D33, SMC_D-C80_#6_Grism_in.pin_1, R6.Pin_0
  N16: EtherMega.D34, 12vRelay7.COIL2
  N17: EtherMega.D35, SMC_D-C80_#7_Grism_Rotation_Pos_0.pin_1, R7.Pin_0
  N18: EtherMega.D36, 12vRelay8.COIL2
  N19: EtherMega.D37, SMC_D-C80_#8_Grism_Rotation_Pos_1.pin_1, R8.Pin_0
  N20: 12vRelay1.NO, Solenoid_Mirror.pin2
  N21: 12vRelay1.MAIN, 12vRelay2.MAIN, 12vRelay3.MAIN, 12vRelay4.MAIN, 12vRelay5.MAIN, 12vRelay6.MAIN, 12vRelay7.MAIN, 12vRelay8.MAIN, 13vAdjustablePowerSupply.V-
  N22: 12vRelay2.NO, Solenoid_Slit.pin2
  N23: 12vRelay3.NO, Solenoid_Grism.pin2
  N24: 12vRelay4.NO, Solenoid_Grism_Rotate.pin2
  N25: 12vRelay5.NO, Tungsten_Lamp.pin2
  N26: 13vAdjustablePowerSupply.V+, Solenoid_Mirror.pin1, Solenoid_Slit.pin1, Solenoid_Grism.pin1, Solenoid_Grism_Rotate.pin1, Tungsten_Lamp.pin1
  N27: Arc_Lamp_Mains_Relay_CARLO_GAVAZZI_-_RGS1A23D25KKE.NO, Arc_Lamp.pin2
  N28: Arc_Lamp_Mains_Relay_CARLO_GAVAZZI_-_RGS1A23D25KKE.MAIN, Mains_Power_plug.GND
  N29: Arc_Lamp.pin1, Mains_Power_plug.VCC

notes:
  12vrelay1 to 12vrelay8 are all mounted on the Hobbytronics 12V relay module. This has opto isolated inputs (now shown here). The 12v and 5v grounds can be tied together or separate :- we will try separate grounds first
  IN= HIGH, OUT = LOW

custom parts:
  Filament Lamp: A filament lamp
